// Logisim project thing.circ as structural Verilog: 3 circuits, main circuit CPU
module CPU (
);

  wire and_5_out, button_1_out, CLK, clock_1_out, I_JMP, I_LW, I_SW, JMP, not_1_out, RST, t_ff_1_q;
  wire [2:0] alu_1_neg, and_6_out, and_7_out, bit_extender_2_out, I2;
  wire [3:0] BA, BB, BD, INST, multiplexer_2_out;
  wire [15:0] adder_1_out, ALUOUT, bit_extender_1_out, DIN, multiplexer_1_out, multiplexer_3_out, PC, RA,
       RAMOUT, RB;

  Clock clock_1 (.out(clock_1_out));
  T_Flip_Flop t_ff_1 (.T(1'b1), .clk(button_1_out), .Q(t_ff_1_q));  // open: Qn, reset, preset
  Button button_1 (.out(button_1_out));
  Button button_2 (.out(RST));
  and and_1 (I_LW, INST[0], ~INST[1], ~INST[2], ~INST[3]);  // AND_Gate
  and and_2 (I_SW, INST[0], ~INST[1], ~INST[2], INST[3]);  // AND_Gate
  and and_3 (I_JMP, INST[0], INST[1], INST[2], ~INST[3]);  // AND_Gate
  and and_4 (CLK, clock_1_out, t_ff_1_q);
  assign bit_extender_1_out = {{8{BD[3]}}, {BD, BA}};  // Bit_Extender bit_extender_1
  and and_5 (and_5_out, BB[3], JMP, I_JMP);
  Adder #(.width(16)) adder_1 (.a(PC), .b(multiplexer_1_out), .out(adder_1_out));  // open: cin, cout
  Multiplexer #(.width(16)) multiplexer_1 (
    .in0(16'h1), .in1(bit_extender_1_out), .out(multiplexer_1_out), .sel(and_5_out));
  Multiplexer #(.width(4)) multiplexer_2 (.in0(BB), .in1(BD), .out(multiplexer_2_out), .sel(I_SW));
  ROM #(.addrWidth(16), .dataWidth(16)) rom_1 (.addr(PC), .data({BB, BA, BD, INST}));
  RegFile regfile_1 (
    .D(DIN), .CLK(CLK), .RST(RST), .DSEL(BD), .PCIN(adder_1_out), .ASEL(BA), .BSEL(multiplexer_2_out),
    .PCOUT(PC), .A(RA), .B(RB));  // open: EN
  assign bit_extender_2_out = {{2{INST[3]}}, INST[3]};  // Bit_Extender bit_extender_2
  assign and_6_out = INST[2:0] & ~bit_extender_2_out;  // AND_Gate and_6, 3 bits wide
  Multiplexer #(.width(16)) multiplexer_3 (.in0(RB), .out(multiplexer_3_out));  // open: in1, sel
  not not_1 (not_1_out, INST[3]);
  RAM #(.addrWidth(16), .dataWidth(16), .enables("line")) ram_1 (
    .addr(ALUOUT), .we(I_SW), .clk(CLK), .din(ALUOUT), .dout(RAMOUT));
  ALU alu_1 (
    .A(RA), .B(multiplexer_3_out), .OP(and_6_out), .OUT(ALUOUT), .NEG(alu_1_neg[0]), .ZERO(alu_1_neg[1]),
    .POS(alu_1_neg[2]));
  Register #(.width(3)) register_1 (.D(alu_1_neg), .en(not_1_out), .clk(CLK), .Q(I2), .clr(RST));
  Multiplexer #(.width(16)) multiplexer_4 (.in0(ALUOUT), .in1(RAMOUT), .out(DIN), .sel(I_LW));
  assign and_7_out = BB[2:0] & I2;  // AND_Gate and_7, 3 bits wide
  or or_1 (JMP, and_7_out[0], and_7_out[1], and_7_out[2]);

  // Other names for the same wires on the sheet: OPCODE[3:0] = INST; INST[15:4] = {BB, BA, BD}

  // Notes on the sheet:
  //   contents of rom_1 (hex, n*v repeats v):
  //   29*0 10
endmodule

module RegFile (
  input  CLK,
  input  RST,
  input  [15:0] D,
  input  [15:0] PCIN,
  input  EN,
  input  [3:0] DSEL,
  input  [3:0] ASEL,
  input  [3:0] BSEL,
  output [15:0] A,
  output [15:0] B,
  output [15:0] PCOUT
);

  wire demultiplexer_1_out1, demultiplexer_1_out2, demultiplexer_1_out3, demultiplexer_1_out4,
       demultiplexer_1_out5, demultiplexer_1_out6, demultiplexer_1_out7, demultiplexer_1_out8,
       demultiplexer_1_out9, demultiplexer_1_out10, demultiplexer_1_out11, demultiplexer_1_out12,
       demultiplexer_1_out13, demultiplexer_1_out14, demultiplexer_1_out15;
  wire [15:0] multiplexer_1_out, O2, O3, O4, O5, O6, O7, O8, O9, OA, OB, OC, OD, OE, OF;

  Demultiplexer #(.select(4)) demultiplexer_1 (
    .out1(demultiplexer_1_out1), .out2(demultiplexer_1_out2), .out3(demultiplexer_1_out3),
    .out4(demultiplexer_1_out4), .out5(demultiplexer_1_out5), .out6(demultiplexer_1_out6),
    .out7(demultiplexer_1_out7), .out8(demultiplexer_1_out8), .out9(demultiplexer_1_out9),
    .out10(demultiplexer_1_out10), .out11(demultiplexer_1_out11), .out12(demultiplexer_1_out12),
    .out13(demultiplexer_1_out13), .out14(demultiplexer_1_out14), .out15(demultiplexer_1_out15), .in(EN),
    .sel(DSEL));  // open: out0
  Multiplexer #(.width(16)) multiplexer_1 (.in0(PCIN), .in1(D), .out(multiplexer_1_out), .sel(demultiplexer_1_out1));
  Register #(.width(16)) register_1 (.D(D), .en(demultiplexer_1_out15), .Q(OF), .clk(CLK), .clr(RST));
  Register #(.width(16)) register_2 (.D(multiplexer_1_out), .en(1'b1), .Q(PCOUT), .clk(CLK), .clr(RST));
  Register #(.width(16)) register_3 (.D(D), .en(demultiplexer_1_out14), .Q(OE), .clk(CLK), .clr(RST));
  Multiplexer #(.select(4), .width(16)) multiplexer_2 (
    .in0({16{1'b0}}), .in1(PCOUT), .in2(O2), .in3(O3), .in4(O4), .in5(O5), .in6(O6), .in7(O7), .in8(O8),
    .in9(O9), .in10(OA), .in11(OB), .in12(OC), .in13(OD), .in14(OE), .in15(OF), .out(A), .sel(ASEL));
  Register #(.width(16)) register_4 (.D(D), .en(demultiplexer_1_out2), .Q(O2), .clk(CLK));  // open: clr
  Register #(.width(16)) register_5 (.D(D), .en(demultiplexer_1_out13), .Q(OD), .clk(CLK), .clr(RST));
  Register #(.width(16)) register_6 (.D(D), .en(demultiplexer_1_out3), .Q(O3), .clk(CLK), .clr(RST));
  Register #(.width(16)) register_7 (.D(D), .en(demultiplexer_1_out12), .Q(OC), .clk(CLK), .clr(RST));
  Register #(.width(16)) register_8 (.D(D), .en(demultiplexer_1_out4), .Q(O4), .clk(CLK), .clr(RST));
  Register #(.width(16)) register_9 (.D(D), .en(demultiplexer_1_out11), .Q(OB), .clk(CLK), .clr(RST));
  Register #(.width(16)) register_10 (.D(D), .en(demultiplexer_1_out5), .Q(O5), .clk(CLK), .clr(RST));
  Register #(.width(16)) register_11 (.D(D), .en(demultiplexer_1_out10), .Q(OA), .clk(CLK), .clr(RST));
  Multiplexer #(.select(4), .width(16)) multiplexer_3 (
    .in0({16{1'b0}}), .in1(PCOUT), .in2(O2), .in3(O3), .in4(O4), .in5(O5), .in6(O6), .in7(O7), .in8(O8),
    .in9(O9), .in10(OA), .in11(OB), .in12(OC), .in13(OD), .in14(OE), .in15(OF), .out(B), .sel(BSEL));
  Register #(.width(16)) register_12 (.D(D), .en(demultiplexer_1_out6), .Q(O6), .clk(CLK), .clr(RST));
  Register #(.width(16)) register_13 (.D(D), .en(demultiplexer_1_out9), .Q(O9), .clk(CLK), .clr(RST));
  Register #(.width(16)) register_14 (.D(D), .en(demultiplexer_1_out7), .Q(O7), .clk(CLK), .clr(RST));
  Register #(.width(16)) register_15 (.D(D), .en(demultiplexer_1_out8), .Q(O8), .clk(CLK), .clr(RST));

  // Other names for the same wires on the sheet: O1[15:0] = PCOUT
endmodule

module ALU (
  input  [2:0] OP,
  input  [15:0] A,
  input  [15:0] B,
  output ZERO,
  output POS,
  output NEG,
  output [15:0] OUT
);

  wire [15:0] adder_1_out, and_1_out, bit_extender_1_out, bit_extender_2_out, multiplexer_1_out,
       multiplexer_2_out, or_1_out, shifter_1_out, shifter_2_out, xor_1_out, xor_2_out, xor_3_out;

  assign bit_extender_1_out = {{15{OP[0]}}, OP[0]};  // Bit_Extender bit_extender_1
  assign xor_1_out = B ^ bit_extender_1_out;  // XOR_Gate xor_1, 16 bits wide
  assign bit_extender_2_out = {{15{OP[0]}}, OP[0]};  // Bit_Extender bit_extender_2
  Adder #(.width(16)) adder_1 (.a(A), .b(xor_1_out), .out(adder_1_out), .cin(OP[0]));  // open: cout
  Shifter #(.width(16)) shifter_1 (.in(A), .\dist (B[3:0]), .out(shifter_1_out));
  Shifter #(.shift("lr"), .width(16)) shifter_2 (.in(A), .\dist (B[3:0]), .out(shifter_2_out));
  assign and_1_out = A & B;  // AND_Gate and_1, 16 bits wide
  assign or_1_out = A | B;  // OR_Gate or_1, 16 bits wide
  assign xor_2_out = A ^ B;  // XOR_Gate xor_2, 16 bits wide
  Multiplexer #(.width(16)) multiplexer_1 (
    .in0(shifter_1_out), .in1(shifter_2_out), .out(multiplexer_1_out), .sel(OP[0]));
  assign xor_3_out = and_1_out ^ bit_extender_2_out;  // XOR_Gate xor_3, 16 bits wide
  Multiplexer #(.width(16)) multiplexer_2 (.in0(or_1_out), .in1(xor_2_out), .out(multiplexer_2_out), .sel(OP[0]));
  Multiplexer #(.select(2), .width(16)) multiplexer_3 (
    .in0(adder_1_out), .in1(multiplexer_1_out), .in2(xor_3_out), .in3(multiplexer_2_out),
    .out({NEG, OUT[14:0]}), .sel(OP[2:1]));
  nor nor_1 (ZERO, OUT[0], OUT[1], OUT[2], OUT[3], OUT[4], OUT[5], OUT[6], OUT[7], OUT[8], OUT[9], OUT[10], OUT[11], OUT[12], OUT[13], OUT[14], NEG);
  nor nor_2 (POS, ZERO, NEG);

  assign OUT[15] = NEG;

  // Other names for the same wires on the sheet: OP12[1:0] = OP[2:1]
endmodule
